# Fritzing sketch ButtonBoard (saved by Fritzing 0.9.5d)
stripboards: 1

parts:
  J1 = female pin header, 4 pins [form="♀ (female)"]
  S1 = Pushbutton [package="[THT]"]
  S2 = Pushbutton [package="[THT]"]
  S3 = Pushbutton [package="[THT]"]

nets:
  N1: J1.pin1, S1.Pin_1, S1.Pin_2
  N2: J1.pin2, S2.Pin_1, S2.Pin_2
  N3: J1.pin3, S3.Pin_1, S3.Pin_2
  N4: J1.pin4, S1.Pin_3, S1.Pin_4, S2.Pin_3, S2.Pin_4, S3.Pin_3, S3.Pin_4

notes:
  This is a small "daughter" board containing the three push buttons. It can be made from the scrap when the main board is cut down. It just contains the three micro push buttons, with a piece of 4 conductor ribbon cable and a female header (IDC) connector. You'll want to drill two holes for mounting screws and then drill holes in the box lid for the switches and the mounting screws.
