# Fritzing sketch ReflowOven2 (saved by Fritzing 0.9.5d)
breadboards: 1

parts:
  Part1 = Adafruit Feather M0 Express [part_number="Adafruit #3403"]
  IC1 = IC, DIP package, 14 pins [chip_label=AD595AQ]
  J1 = Camdenboss CTB0158-2 [part_number=Therm package=THT]
  J2 = Screw terminal - 2 pins [part_number="+5 Power" package=THT]
  J3 = Screw terminal - 2 pins [part_number=Relay package=THT]
  J4 = male pin header, 2 pins [form="♂ (male)" part_number=Buzzer]
  J5 = male pin header, 10 pins [form="♂ (male)" part_number=LCD1]
  J6 = male pin header, 4 pins [form="♂ (male)" part_number=Switches]
  R1 = Resistor [tolerance=±5% resistance=10k package=THT]
  C1 = Ceramic Capacitor [capacitance=0.1mF package="100 mil [THT, multilayer]"]
  C2 = Electrolytic Capacitor [capacitance=47µF package="100 mil [THT, electrolytic]"]

nets:
  GND: Part1.GND, IC1.pin7, IC1.pin10, IC1.pin13, J2.pin1, J3.pin2, J4.pin2, J5.pin10, J6.pin4, R1.Pin_1, C1.1, C2.-
  N1: Part1.MISO, J5.pin2
  N2: Part1.MOSI, J5.pin4
  N3: Part1.SCK, J5.pin3
  N4: Part1.A3, J6.pin3
  N5: Part1.A2, J6.pin2
  N6: Part1.A1, J6.pin1
  N7: Part1.A0, IC1.pin8, IC1.pin9
  3.3V: Part1.+3V3
  5V: Part1.VBAT, IC1.pin11, J2.pin2, J5.pin9, C1.0, C2.+
  N8: Part1.D13, J3.pin1, R1.Pin_0
  N9: Part1.D12, J4.pin1
  N10: Part1.D11, J5.pin8
  N11: Part1.D10, J5.pin7
  N12: Part1.D6, J5.pin5
  N13: Part1.D5, J5.pin1
  N14: IC1.pin1, J1.pin1
  N15: IC1.pin14, J1.pin2

notes:
  I used a BusBoard Prototype Systems BR1 solderable breadboard. I expect an Adafruit full size Protoboard woul also work. In either case the board will need to be cut down to fit the box and new mounting holes drilled. Some of the wires should go on the underside, especially those that might otherwise go over the top of components. It is recomended that female headers be used with the Feather to allow for removing it if needed. The large screw terminal is for the thermocouple -- plus(+) is to the left as viewed from the top with the feather to the right. The small scree terminal next to the large screw terminal is the 5 volt power input, with plus (+) the terminal farther from the center of the board. The other small screw terminal is for the toaster oven SSR in the lower box. The 4-pin header next to the thermocouple is for the push button switches (ground, upper button, middle button, bottom button). The 10-pin header is for the LCD and the 2-pin header is for the buzzer.

custom parts:
  Adafruit Feather M0 Express: We love all our Feathers equally, but this Feather is very special. It's our first Feather that is specifically designed for use with CircuitPython! CircuitPython is our beginner-oriented flavor of MicroPython - and as the name hints at, its a small but full-featured version of the popular Python programming language specifically for use with circuitry and electronics. That doesn't mean you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
